# Fritzing sketch RTC (saved by Fritzing 1.0.2b)
breadboards: 1

parts:
  Part1 = Arduino Uno (Rev3) - ICSP
  OLED_I2C1 = OLED 128x64 I2C Monochrome Display
  ZS-042_RTC1 = ZS-042 RTC Module  # not connected

nets:
  N1: Part1.A4/SDA, OLED_I2C1.SDA
  N2: Part1.A5/SCL, OLED_I2C1.SCK
  5V: Part1.5V, OLED_I2C1.VDD
  GND: Part1.GND, OLED_I2C1.GND
